# Fritzing sketch Flex Sensor Schematic (saved by Fritzing 0.9.3b)
breadboards: 1

parts:
  Part1 = Arduino Uno (Rev3)
  R1 = Basic Flex Resistor
  R2 = Resistor [tolerance=±5% resistance=220 package=THT]

nets:
  N1: Part1.A0, R1.pin_1, R2.Pin_0
  N2: Part1.5V, R1.Pin_2
  N3: Part1.GND, R2.Pin_1

notes:
  10k resistor
