# Fritzing sketch Vibration_Sensor_Test_Schem (saved by Fritzing 0.9.3b)

parts:
  S1 = TILT-SWITCH-SW-200D [package=reed_switch_plastic]
  Part1 = Arduino Uno (Rev3)

nets:
  N1: S1.1, Part1.GND
  N2: S1.2, Part1.D2
